// Logisim project Spark 16.circ as structural Verilog: 41 circuits, main circuit main
module main (
);

  wire and_1_out, CLK_out, jc16_cpu_1_ldram, jc16_cpu_1_oclk, jc16_cpu_1_run_clk, jc16_cpu_1_stram;
  wire [15:0] adder_1_out, adder_2_out, jc16_cpu_1_o_pin0, jc16_cpu_1_ram_addr, jc16_cpu_1_ram_val_st,
       jc16_cpu_1_rom_addr, ram_1_dout, register_1_q;
  wire [23:0] rom_1_data, rom_2_data;

  ROM #(.addrWidth(16), .dataWidth(24)) rom_1 (.addr(jc16_cpu_1_rom_addr), .data(rom_1_data));
  ROM #(.addrWidth(16), .dataWidth(24)) rom_2 (.addr(adder_1_out), .data(rom_2_data));
  Adder #(.width(16)) adder_1 (.a(jc16_cpu_1_rom_addr), .b(16'h1), .out(adder_1_out));  // open: cin, cout
  Register #(.width(16)) register_1 (.D(adder_2_out), .en(and_1_out), .clk(and_1_out), .Q(register_1_q));  // open: clr
  Adder #(.width(16)) adder_2 (.a(register_1_q), .b(16'h1), .out(adder_2_out));  // open: cin, cout
  Clock CLK (.out(CLK_out));
  and and_1 (and_1_out, CLK_out, jc16_cpu_1_run_clk);
  JC16_CPU jc16_cpu_1 (
    .CLK(and_1_out), .INSTRUCTION(rom_1_data), .SECOND_INSTR(rom_2_data), .RAM_VAL_LD(ram_1_dout),
    .RAM_ADDR(jc16_cpu_1_ram_addr), .ROM_ADDR(jc16_cpu_1_rom_addr), .LDRAM(jc16_cpu_1_ldram),
    .OCLK(jc16_cpu_1_oclk), .RUN_CLK(jc16_cpu_1_run_clk), .STRAM(jc16_cpu_1_stram),
    .RAM_VAL_ST(jc16_cpu_1_ram_val_st), .O_PIN0(jc16_cpu_1_o_pin0));  // open: I_PIN0, I_PIN1, I_PIN2, I_PIN3, O_PIN1, O_PIN2, O_PIN3
  RAM #(.addrWidth(16), .dataWidth(16)) ram_1 (
    .addr(jc16_cpu_1_ram_addr), .we(jc16_cpu_1_stram), .oe(jc16_cpu_1_ldram), .din(jc16_cpu_1_ram_val_st),
    .dout(ram_1_dout));  // open: clk
  TTY tty_1 (.data(jc16_cpu_1_o_pin0[6:0]), .clk(jc16_cpu_1_oclk), .we(jc16_cpu_1_oclk));  // open: clr

  // Notes on the sheet:
  //   contents of rom_1 (hex, n*v repeats v):
  //   c50000 c40048 e58000 b80000 c40065 e58000 b80000 c4006c e58000 b80000 c4006c e58000 b80000 c4006f
  //   e58000 b80000 c40020 e58000 b80000 c40077 e58000 b80000 c4006f e58000 b80000 c40072 e58000 b80000
  //   c4006c e58000 b80000 c40064 e58000 b80000 f80000
  //   contents of rom_2 (hex, n*v repeats v):
  //   c50000 c60001 c40048 e58000 d44000 c40001 e4c000 c40000 e4c000 cc4000 c40065 e58000 d44000 c40001
  //   e4c000 c40000 e4c000 cc4000 c4006c e58000 d44000 c40001 e4c000 c40000 e4c000 cc4000 c4006c e58000
  //   d44000 c40001 e4c000 c40000 e4c000 cc4000 c4006f e58000 d44000 c40001 e4c000 c40000 e4c000 cc4000
  //   c40020 e58000 d44000 c40001 e4c000 c40000 e4c000 cc4000 c40077 e58000 d44000 c40001 e4c000 c40000
  //   e4c000 cc4000 c4006f e58000 d44000 c40001 e4c000 c40000 e4c000 cc4000 c40072 e58000 d44000 c40001
  //   e4c000 c40000 e4c000 cc4000 c4006c e58000 d44000 c40001 e4c000 c40000 e4c000 cc4000 c40064 e58000
  //   d44000 c40001 e4c000 c40000 e4c000 cc4000 f80000 c40000 e68000 cc4000 f80000
endmodule

module JCS1_FullAdder (
  input  A,
  input  B,
  input  CarryIn,
  output Sum,
  output CarryOut
);

  wire and_1_out, and_2_out, xor_1_out;

  xor xor_1 (xor_1_out, A, B);
  and and_1 (and_1_out, B, A);
  xor xor_2 (Sum, xor_1_out, CarryIn);
  and and_2 (and_2_out, CarryIn, xor_1_out);
  or or_1 (CarryOut, and_2_out, and_1_out);
endmodule

module JCS1_16bitAdder (
  input  [15:0] A,
  input  [15:0] B,
  output [15:0] R,
  output CarryOut
);

  wire jcs1_fulladder_1_carryout, jcs1_fulladder_2_carryout, jcs1_fulladder_3_carryout,
       jcs1_fulladder_4_carryout, jcs1_fulladder_5_carryout, jcs1_fulladder_6_carryout,
       jcs1_fulladder_7_carryout, jcs1_fulladder_8_carryout, jcs1_fulladder_9_carryout,
       jcs1_fulladder_10_carryout, jcs1_fulladder_11_carryout, jcs1_fulladder_12_carryout,
       jcs1_fulladder_13_carryout, jcs1_fulladder_14_carryout, jcs1_fulladder_15_carryout;

  JCS1_FullAdder jcs1_fulladder_1 (
    .A(A[0]), .B(B[0]), .CarryIn(1'b0), .Sum(R[0]), .CarryOut(jcs1_fulladder_1_carryout));
  JCS1_FullAdder jcs1_fulladder_2 (
    .A(A[1]), .B(B[1]), .CarryIn(jcs1_fulladder_1_carryout), .Sum(R[1]), .CarryOut(jcs1_fulladder_2_carryout));
  JCS1_FullAdder jcs1_fulladder_3 (
    .A(A[2]), .B(B[2]), .CarryIn(jcs1_fulladder_2_carryout), .Sum(R[2]), .CarryOut(jcs1_fulladder_3_carryout));
  JCS1_FullAdder jcs1_fulladder_4 (
    .A(A[3]), .B(B[3]), .CarryIn(jcs1_fulladder_3_carryout), .Sum(R[3]), .CarryOut(jcs1_fulladder_4_carryout));
  JCS1_FullAdder jcs1_fulladder_5 (
    .A(A[4]), .B(B[4]), .CarryIn(jcs1_fulladder_4_carryout), .Sum(R[4]), .CarryOut(jcs1_fulladder_5_carryout));
  JCS1_FullAdder jcs1_fulladder_6 (
    .A(A[5]), .B(B[5]), .CarryIn(jcs1_fulladder_5_carryout), .Sum(R[5]), .CarryOut(jcs1_fulladder_6_carryout));
  JCS1_FullAdder jcs1_fulladder_7 (
    .A(A[6]), .B(B[6]), .CarryIn(jcs1_fulladder_6_carryout), .Sum(R[6]), .CarryOut(jcs1_fulladder_7_carryout));
  JCS1_FullAdder jcs1_fulladder_8 (
    .A(A[7]), .B(B[7]), .CarryIn(jcs1_fulladder_7_carryout), .Sum(R[7]), .CarryOut(jcs1_fulladder_8_carryout));
  JCS1_FullAdder jcs1_fulladder_9 (
    .A(A[8]), .B(B[8]), .CarryIn(jcs1_fulladder_8_carryout), .Sum(R[8]), .CarryOut(jcs1_fulladder_9_carryout));
  JCS1_FullAdder jcs1_fulladder_10 (
    .A(A[9]), .B(B[9]), .CarryIn(jcs1_fulladder_9_carryout), .Sum(R[9]), .CarryOut(jcs1_fulladder_10_carryout));
  JCS1_FullAdder jcs1_fulladder_11 (
    .A(A[10]), .B(B[10]), .CarryIn(jcs1_fulladder_10_carryout), .Sum(R[10]),
    .CarryOut(jcs1_fulladder_11_carryout));
  JCS1_FullAdder jcs1_fulladder_12 (
    .A(A[11]), .B(B[11]), .CarryIn(jcs1_fulladder_11_carryout), .Sum(R[11]),
    .CarryOut(jcs1_fulladder_12_carryout));
  JCS1_FullAdder jcs1_fulladder_13 (
    .A(A[12]), .B(B[12]), .CarryIn(jcs1_fulladder_12_carryout), .Sum(R[12]),
    .CarryOut(jcs1_fulladder_13_carryout));
  JCS1_FullAdder jcs1_fulladder_14 (
    .A(A[13]), .B(B[13]), .CarryIn(jcs1_fulladder_13_carryout), .Sum(R[13]),
    .CarryOut(jcs1_fulladder_14_carryout));
  JCS1_FullAdder jcs1_fulladder_15 (
    .A(A[14]), .B(B[14]), .CarryIn(jcs1_fulladder_14_carryout), .Sum(R[14]),
    .CarryOut(jcs1_fulladder_15_carryout));
  JCS1_FullAdder jcs1_fulladder_16 (
    .A(A[15]), .B(B[15]), .CarryIn(jcs1_fulladder_15_carryout), .Sum(R[15]), .CarryOut(CarryOut));
endmodule

module JCS1_FullSubtractor (
  input  A,
  input  B,
  input  BorrowIn,
  output Diff,
  output BorrowOut
);

  wire and_1_out, not_1_out, or_1_out, or_2_out, xor_1_out;

  xor xor_1 (xor_1_out, A, B);
  not not_1 (not_1_out, A);
  and and_1 (and_1_out, B, BorrowIn);
  xor xor_2 (Diff, xor_1_out, BorrowIn);
  or or_1 (or_1_out, not_1_out, and_1_out);
  or or_2 (or_2_out, B, BorrowIn);
  and and_2 (BorrowOut, or_1_out, or_2_out);
endmodule

module JCS1_16bitSubtractor (
  input  [15:0] A,
  input  [15:0] B,
  output [15:0] R,
  output CarryOut
);

  wire jcs1_fullsubtractor_1_borrowout, jcs1_fullsubtractor_2_borrowout, jcs1_fullsubtractor_3_borrowout,
       jcs1_fullsubtractor_4_borrowout, jcs1_fullsubtractor_5_borrowout, jcs1_fullsubtractor_6_borrowout,
       jcs1_fullsubtractor_7_borrowout, jcs1_fullsubtractor_8_borrowout, jcs1_fullsubtractor_9_borrowout,
       jcs1_fullsubtractor_10_borrowout, jcs1_fullsubtractor_11_borrowout, jcs1_fullsubtractor_12_borrowout,
       jcs1_fullsubtractor_13_borrowout, jcs1_fullsubtractor_14_borrowout, jcs1_fullsubtractor_15_borrowout;

  JCS1_FullSubtractor jcs1_fullsubtractor_1 (
    .A(A[0]), .B(B[0]), .BorrowIn(1'b0), .Diff(R[0]), .BorrowOut(jcs1_fullsubtractor_1_borrowout));
  JCS1_FullSubtractor jcs1_fullsubtractor_2 (
    .A(A[1]), .B(B[1]), .BorrowIn(jcs1_fullsubtractor_1_borrowout), .Diff(R[1]),
    .BorrowOut(jcs1_fullsubtractor_2_borrowout));
  JCS1_FullSubtractor jcs1_fullsubtractor_3 (
    .A(A[2]), .B(B[2]), .BorrowIn(jcs1_fullsubtractor_2_borrowout), .Diff(R[2]),
    .BorrowOut(jcs1_fullsubtractor_3_borrowout));
  JCS1_FullSubtractor jcs1_fullsubtractor_4 (
    .A(A[3]), .B(B[3]), .BorrowIn(jcs1_fullsubtractor_3_borrowout), .Diff(R[3]),
    .BorrowOut(jcs1_fullsubtractor_4_borrowout));
  JCS1_FullSubtractor jcs1_fullsubtractor_5 (
    .A(A[4]), .B(B[4]), .BorrowIn(jcs1_fullsubtractor_4_borrowout), .Diff(R[4]),
    .BorrowOut(jcs1_fullsubtractor_5_borrowout));
  JCS1_FullSubtractor jcs1_fullsubtractor_6 (
    .A(A[5]), .B(B[5]), .BorrowIn(jcs1_fullsubtractor_5_borrowout), .Diff(R[5]),
    .BorrowOut(jcs1_fullsubtractor_6_borrowout));
  JCS1_FullSubtractor jcs1_fullsubtractor_7 (
    .A(A[6]), .B(B[6]), .BorrowIn(jcs1_fullsubtractor_6_borrowout), .Diff(R[6]),
    .BorrowOut(jcs1_fullsubtractor_7_borrowout));
  JCS1_FullSubtractor jcs1_fullsubtractor_8 (
    .A(A[7]), .B(B[7]), .BorrowIn(jcs1_fullsubtractor_7_borrowout), .Diff(R[7]),
    .BorrowOut(jcs1_fullsubtractor_8_borrowout));
  JCS1_FullSubtractor jcs1_fullsubtractor_9 (
    .A(A[8]), .B(B[8]), .BorrowIn(jcs1_fullsubtractor_8_borrowout), .Diff(R[8]),
    .BorrowOut(jcs1_fullsubtractor_9_borrowout));
  JCS1_FullSubtractor jcs1_fullsubtractor_10 (
    .A(A[9]), .B(B[9]), .BorrowIn(jcs1_fullsubtractor_9_borrowout), .Diff(R[9]),
    .BorrowOut(jcs1_fullsubtractor_10_borrowout));
  JCS1_FullSubtractor jcs1_fullsubtractor_11 (
    .A(A[10]), .B(B[10]), .BorrowIn(jcs1_fullsubtractor_10_borrowout), .Diff(R[10]),
    .BorrowOut(jcs1_fullsubtractor_11_borrowout));
  JCS1_FullSubtractor jcs1_fullsubtractor_12 (
    .A(A[11]), .B(B[11]), .BorrowIn(jcs1_fullsubtractor_11_borrowout), .Diff(R[11]),
    .BorrowOut(jcs1_fullsubtractor_12_borrowout));
  JCS1_FullSubtractor jcs1_fullsubtractor_13 (
    .A(A[12]), .B(B[12]), .BorrowIn(jcs1_fullsubtractor_12_borrowout), .Diff(R[12]),
    .BorrowOut(jcs1_fullsubtractor_13_borrowout));
  JCS1_FullSubtractor jcs1_fullsubtractor_14 (
    .A(A[13]), .B(B[13]), .BorrowIn(jcs1_fullsubtractor_13_borrowout), .Diff(R[13]),
    .BorrowOut(jcs1_fullsubtractor_14_borrowout));
  JCS1_FullSubtractor jcs1_fullsubtractor_15 (
    .A(A[14]), .B(B[14]), .BorrowIn(jcs1_fullsubtractor_14_borrowout), .Diff(R[14]),
    .BorrowOut(jcs1_fullsubtractor_15_borrowout));
  JCS1_FullSubtractor jcs1_fullsubtractor_16 (
    .A(A[15]), .B(B[15]), .BorrowIn(jcs1_fullsubtractor_15_borrowout), .Diff(R[15]), .BorrowOut(CarryOut));
endmodule

module JCS1_ALU (
  input  [3:0] F,
  input  [15:0] A,
  input  [15:0] B,
  output [15:0] R,
  output Carry
);

  wire jcs1_16bitadder_1_carryout, jcs1_16bitsubtractor_1_carryout;
  wire [15:0] jc16_16bit_equal_1_r, jc16_16bit_greaterthan_1_r, jc16_16bit_lessthan_1_r,
       jc16_16bit_lshift_1_r, jc16_16bit_rshift_1_r, jcs1_16bit_and_1_r, jcs1_16bit_nand_1_r,
       jcs1_16bit_nor_1_r, jcs1_16bit_not_1_r, jcs1_16bit_or_1_r, jcs1_16bit_xor_1_r, jcs1_16bitadder_1_r,
       jcs1_16bitsubtractor_1_r;
  wire [31:0] demultiplexer_1_out0, demultiplexer_1_out1, demultiplexer_1_out2, demultiplexer_1_out3,
       demultiplexer_1_out4, demultiplexer_1_out5, demultiplexer_1_out6, demultiplexer_1_out7,
       demultiplexer_1_out8, demultiplexer_1_out9, demultiplexer_1_out10, demultiplexer_1_out11,
       demultiplexer_1_out12, demultiplexer_1_out15;

  Demultiplexer #(.select(4), .width(32)) demultiplexer_1 (
    .out0(demultiplexer_1_out0), .out1(demultiplexer_1_out1), .out2(demultiplexer_1_out2),
    .out3(demultiplexer_1_out3), .out4(demultiplexer_1_out4), .out5(demultiplexer_1_out5),
    .out6(demultiplexer_1_out6), .out7(demultiplexer_1_out7), .out8(demultiplexer_1_out8),
    .out9(demultiplexer_1_out9), .out10(demultiplexer_1_out10), .out11(demultiplexer_1_out11),
    .out12(demultiplexer_1_out12), .out15(demultiplexer_1_out15), .in({B, A}), .sel(F));  // open: out13, out14
  JCS1_16bitAdder jcs1_16bitadder_1 (
    .A(demultiplexer_1_out0[15:0]), .B(demultiplexer_1_out0[31:16]), .R(jcs1_16bitadder_1_r),
    .CarryOut(jcs1_16bitadder_1_carryout));
  JCS1_16bitSubtractor jcs1_16bitsubtractor_1 (
    .A(demultiplexer_1_out1[15:0]), .B(demultiplexer_1_out1[31:16]), .R(jcs1_16bitsubtractor_1_r),
    .CarryOut(jcs1_16bitsubtractor_1_carryout));
  JCS1_16bit_AND jcs1_16bit_and_1 (
    .A(demultiplexer_1_out2[15:0]), .B(demultiplexer_1_out2[31:16]), .R(jcs1_16bit_and_1_r));
  JCS1_16bit_NOT jcs1_16bit_not_1 (.A(demultiplexer_1_out3[15:0]), .R(jcs1_16bit_not_1_r));
  JCS1_16bit_OR jcs1_16bit_or_1 (
    .A(demultiplexer_1_out4[15:0]), .B(demultiplexer_1_out4[31:16]), .R(jcs1_16bit_or_1_r));
  JCS1_16bit_XOR jcs1_16bit_xor_1 (
    .A(demultiplexer_1_out5[15:0]), .B(demultiplexer_1_out5[31:16]), .R(jcs1_16bit_xor_1_r));
  JCS1_16bit_NAND jcs1_16bit_nand_1 (
    .A(demultiplexer_1_out6[15:0]), .B(demultiplexer_1_out6[31:16]), .R(jcs1_16bit_nand_1_r));
  JCS1_16bit_NOR jcs1_16bit_nor_1 (
    .A(demultiplexer_1_out7[15:0]), .B(demultiplexer_1_out7[31:16]), .R(jcs1_16bit_nor_1_r));
  JC16_16bit_LShift jc16_16bit_lshift_1 (
    .A(demultiplexer_1_out8[15:0]), .B(demultiplexer_1_out8[31:16]), .R(jc16_16bit_lshift_1_r));
  JC16_16bit_RShift jc16_16bit_rshift_1 (
    .A(demultiplexer_1_out9[15:0]), .B(demultiplexer_1_out9[31:16]), .R(jc16_16bit_rshift_1_r));
  JC16_16bit_GreaterThan jc16_16bit_greaterthan_1 (
    .A(demultiplexer_1_out10[15:0]), .B(demultiplexer_1_out10[31:16]), .R(jc16_16bit_greaterthan_1_r));
  JC16_16bit_LessThan jc16_16bit_lessthan_1 (
    .A(demultiplexer_1_out11[15:0]), .B(demultiplexer_1_out11[31:16]), .R(jc16_16bit_lessthan_1_r));
  JC16_16bit_Equal jc16_16bit_equal_1 (
    .A(demultiplexer_1_out12[15:0]), .B(demultiplexer_1_out12[31:16]), .R(jc16_16bit_equal_1_r));
  Multiplexer #(.select(4), .width(16)) multiplexer_1 (
    .in0(jcs1_16bitadder_1_r), .in1(jcs1_16bitsubtractor_1_r), .in2(jcs1_16bit_and_1_r),
    .in3(jcs1_16bit_not_1_r), .in4(jcs1_16bit_or_1_r), .in5(jcs1_16bit_xor_1_r), .in6(jcs1_16bit_nand_1_r),
    .in7(jcs1_16bit_nor_1_r), .in8(jc16_16bit_lshift_1_r), .in9(jc16_16bit_rshift_1_r),
    .in10(jc16_16bit_greaterthan_1_r), .in11(jc16_16bit_lessthan_1_r), .in12(jc16_16bit_equal_1_r),
    .in15(demultiplexer_1_out15[15:0]), .out(R), .sel(F));  // open: in13, in14
  or or_1 (Carry, jcs1_16bitadder_1_carryout, jcs1_16bitsubtractor_1_carryout);
endmodule

module JCS1_8bit_Switch (
  input  [7:0] I,
  input  Activate,
  output [7:0] R
);

  and and_1 (R[0], I[0], Activate);
  and and_2 (R[1], I[1], Activate);
  and and_3 (R[2], I[2], Activate);
  and and_4 (R[3], I[3], Activate);
  and and_5 (R[4], I[4], Activate);
  and and_6 (R[5], I[5], Activate);
  and and_7 (R[6], I[6], Activate);
  and and_8 (R[7], I[7], Activate);
endmodule

module JCS1_16bit_Switch (
  input  [15:0] I,
  input  Activate,
  output [15:0] R0
);

  JCS1_8bit_Switch jcs1_8bit_switch_1 (.I(I[7:0]), .Activate(Activate), .R(R0[7:0]));
  JCS1_8bit_Switch jcs1_8bit_switch_2 (.I(I[15:8]), .Activate(Activate), .R(R0[15:8]));
endmodule

module JCS1_16bit_AND (
  input  [15:0] A,
  input  [15:0] B,
  output [15:0] R
);

  assign R = A & B;  // AND_Gate and_1, 16 bits wide
endmodule

module JCS1_16bit_OR (
  input  [15:0] A,
  input  [15:0] B,
  output [15:0] R
);

  assign R = A | B;  // OR_Gate or_1, 16 bits wide
endmodule

module JCS1_16bit_NOT (
  input  [15:0] A,
  output [15:0] R
);

  assign R = ~A;  // NOT_Gate not_1, 16 bits wide
endmodule

module JCS1_16bit_XOR (
  input  [15:0] A,
  input  [15:0] B,
  output [15:0] R
);

  assign R = A ^ B;  // XOR_Gate xor_1, 16 bits wide
endmodule

module JCS1_16bit_NAND (
  input  [15:0] A,
  input  [15:0] B,
  output [15:0] R
);

  assign R = ~(A & B);  // NAND_Gate nand_1, 16 bits wide
endmodule

module JCS1_16bit_NOR (
  input  [15:0] A,
  input  [15:0] B,
  output [15:0] R
);

  assign R = ~(A | B);  // NOR_Gate nor_1, 16 bits wide
endmodule

module JCS1_1bit_SR_Latch (
  input  S,
  input  R,
  output Q
);

  wire nor_1_out;

  nor nor_1 (nor_1_out, S, Q);
  nor nor_2 (Q, nor_1_out, R);
endmodule

module JCS1_1bit_S_Latch (
  input  V,
  input  CLK,
  output out_3
);

  wire and_1_out, and_2_out, not_1_out;

  not not_1 (not_1_out, V);
  and and_1 (and_1_out, V, CLK);
  and and_2 (and_2_out, not_1_out, CLK);
  JCS1_1bit_SR_Latch jcs1_1bit_sr_latch_1 (.S(and_1_out), .R(and_2_out), .Q(out_3));
endmodule

module JCS1_8bit_Register (
  input  [7:0] D,
  input  CLK,
  input  MUTE,
  input  CLEAR,
  output [7:0] out_5
);

  wire jcs1_1bit_s_latch_1_out_3, jcs1_1bit_s_latch_2_out_3, jcs1_1bit_s_latch_3_out_3,
       jcs1_1bit_s_latch_4_out_3, jcs1_1bit_s_latch_5_out_3, jcs1_1bit_s_latch_6_out_3,
       jcs1_1bit_s_latch_7_out_3, jcs1_1bit_s_latch_8_out_3, not_1_out;
  wire [7:0] multiplexer_1_out;

  Multiplexer #(.width(8)) multiplexer_1 (.in0(D), .in1({8{1'b0}}), .out(multiplexer_1_out), .sel(CLEAR));
  not not_1 (not_1_out, MUTE);
  JCS1_1bit_S_Latch jcs1_1bit_s_latch_1 (.V(multiplexer_1_out[0]), .CLK(CLK), .out_3(jcs1_1bit_s_latch_1_out_3));
  JCS1_1bit_S_Latch jcs1_1bit_s_latch_2 (.V(multiplexer_1_out[1]), .CLK(CLK), .out_3(jcs1_1bit_s_latch_2_out_3));
  JCS1_1bit_S_Latch jcs1_1bit_s_latch_3 (.V(multiplexer_1_out[2]), .CLK(CLK), .out_3(jcs1_1bit_s_latch_3_out_3));
  JCS1_1bit_S_Latch jcs1_1bit_s_latch_4 (.V(multiplexer_1_out[3]), .CLK(CLK), .out_3(jcs1_1bit_s_latch_4_out_3));
  JCS1_1bit_S_Latch jcs1_1bit_s_latch_5 (.V(multiplexer_1_out[4]), .CLK(CLK), .out_3(jcs1_1bit_s_latch_5_out_3));
  JCS1_1bit_S_Latch jcs1_1bit_s_latch_6 (.V(multiplexer_1_out[5]), .CLK(CLK), .out_3(jcs1_1bit_s_latch_6_out_3));
  JCS1_1bit_S_Latch jcs1_1bit_s_latch_7 (.V(multiplexer_1_out[6]), .CLK(CLK), .out_3(jcs1_1bit_s_latch_7_out_3));
  JCS1_1bit_S_Latch jcs1_1bit_s_latch_8 (.V(multiplexer_1_out[7]), .CLK(CLK), .out_3(jcs1_1bit_s_latch_8_out_3));
  and and_1 (out_5[0], jcs1_1bit_s_latch_1_out_3, not_1_out);
  and and_2 (out_5[1], jcs1_1bit_s_latch_2_out_3, not_1_out);
  and and_3 (out_5[2], jcs1_1bit_s_latch_3_out_3, not_1_out);
  and and_4 (out_5[3], jcs1_1bit_s_latch_4_out_3, not_1_out);
  and and_5 (out_5[4], jcs1_1bit_s_latch_5_out_3, not_1_out);
  and and_6 (out_5[5], jcs1_1bit_s_latch_6_out_3, not_1_out);
  and and_7 (out_5[6], jcs1_1bit_s_latch_7_out_3, not_1_out);
  and and_8 (out_5[7], jcs1_1bit_s_latch_8_out_3, not_1_out);
endmodule

module JCS1_Program_Counter (
  input  CLK,
  input  WR,
  input  [15:0] V,
  input  WAS_PARALLEL,
  output [15:0] PR
);

  wire [15:0] adder_1_out, multiplexer_1_out, multiplexer_2_out;

  Multiplexer #(.width(16)) multiplexer_1 (.in0(adder_1_out), .in1(V), .out(multiplexer_1_out), .sel(WR));
  Register #(.width(16)) register_1 (.D(multiplexer_1_out), .en(1'b1), .clk(CLK), .Q(PR));  // open: clr
  Multiplexer #(.width(16)) multiplexer_2 (.in0(16'h1), .in1(16'h2), .out(multiplexer_2_out), .sel(WAS_PARALLEL));
  Adder #(.width(16)) adder_1 (.a(PR), .b(multiplexer_2_out), .out(adder_1_out));  // open: cin, cout
endmodule

module JCS1_Instruction_Decoder (
  input  [23:0] INSTRUCTION,
  output [2:0] REG_DEST,
  output IS_ALU,
  output [2:0] ALU_REG_A,
  output [2:0] ALU_REG_B,
  output [3:0] ALU_INSTR,
  output IS_LDI,
  output [15:0] LDI_VALUE,
  output IS_JMP,
  output IS_JIZ,
  output IS_JNZ,
  output IS_JIC,
  output IS_JNC,
  output [15:0] INSTR_ADDR,
  output IS_OCLK,
  output IS_HALT,
  output IS_LDRAM,
  output IS_STRAM,
  output [15:0] RAM_ADDR,
  output IS_RDPIN,
  output IS_WRPIN,
  output [2:0] PIN_ID_REG,
  output [7:0] ALU_INSTR_BODY,
  output [1:0] ALU_FLAG
);

  wire and_1_out, and_2_out, and_3_out, and_4_out, not_1_out, not_2_out, not_3_out, not_4_out, not_5_out,
       not_6_out, not_7_out, not_8_out, not_9_out, not_10_out, not_11_out, not_12_out, not_13_out,
       not_14_out, not_15_out, not_16_out, not_17_out, not_18_out, not_20_out, or_1_out, or_2_out, or_3_out;

  not not_1 (not_1_out, INSTRUCTION[23]);
  and and_1 (and_1_out, INSTRUCTION[23], not_2_out);
  not not_2 (not_2_out, INSTRUCTION[22]);
  not not_3 (not_3_out, INSTRUCTION[21]);
  and and_2 (and_2_out, and_1_out, not_4_out);
  not not_4 (not_4_out, INSTRUCTION[21]);
  and and_3 (and_3_out, INSTRUCTION[23], INSTRUCTION[22], not_3_out);
  not not_5 (not_5_out, INSTRUCTION[20]);
  not not_6 (not_6_out, INSTRUCTION[19]);
  and and_4 (and_4_out, INSTRUCTION[23], INSTRUCTION[22]);
  not not_7 (not_7_out, INSTRUCTION[21]);
  not not_8 (not_8_out, INSTRUCTION[20]);
  not not_9 (not_9_out, INSTRUCTION[19]);
  not not_10 (not_10_out, INSTRUCTION[20]);
  and and_5 (IS_JMP, and_2_out, not_10_out, not_11_out);
  not not_11 (not_11_out, INSTRUCTION[19]);
  not not_12 (not_12_out, INSTRUCTION[20]);
  and and_6 (IS_JIZ, and_2_out, not_12_out, INSTRUCTION[19]);
  and and_7 (IS_JNZ, and_2_out, INSTRUCTION[20], not_13_out);
  not not_13 (not_13_out, INSTRUCTION[19]);
  and and_8 (IS_JIC, and_2_out, INSTRUCTION[20], INSTRUCTION[19]);
  not not_14 (not_14_out, and_2_out);
  and and_9 (IS_JNC, and_1_out, not_14_out, not_15_out, not_16_out);
  not not_15 (not_15_out, INSTRUCTION[20]);
  not not_16 (not_16_out, INSTRUCTION[19]);
  and and_10 (IS_LDRAM, and_3_out, not_5_out, INSTRUCTION[19]);
  and and_11 (IS_STRAM, and_3_out, INSTRUCTION[20], not_6_out);
  and and_12 (IS_RDPIN, and_4_out, not_7_out, INSTRUCTION[20], INSTRUCTION[19]);
  and and_13 (IS_WRPIN, and_4_out, INSTRUCTION[21], not_8_out, not_9_out);
  not not_17 (not_17_out, INSTRUCTION[23]);
  not not_18 (not_18_out, INSTRUCTION[22]);
  not not_19 (IS_ALU, INSTRUCTION[23]);
  nor nor_1 (IS_LDI, not_17_out, not_18_out, INSTRUCTION[21], INSTRUCTION[20], INSTRUCTION[19]);
  or or_1 (or_1_out, IS_JMP, IS_JIZ, IS_JNZ, IS_JIC);
  or or_2 (or_2_out, IS_LDRAM, IS_STRAM);
  or or_3 (or_3_out, IS_RDPIN, IS_WRPIN);
  not not_20 (not_20_out, INSTRUCTION[22]);
  JC16_3bit_Reg_Switch jc16_3bit_reg_switch_1 (.I(INSTRUCTION[15:13]), .Activate(IS_ALU), .R(ALU_REG_A));
  JC16_3bit_Reg_Switch jc16_3bit_reg_switch_2 (.I(INSTRUCTION[12:10]), .Activate(IS_ALU), .R(ALU_REG_B));
  JC16_4bit_Switch jc16_4bit_switch_1 (.I(INSTRUCTION[22:19]), .Activate(IS_ALU), .R(ALU_INSTR));
  JCS1_16bit_Switch jcs1_16bit_switch_1 (.I(INSTRUCTION[15:0]), .Activate(IS_LDI), .R0(LDI_VALUE));
  JCS1_16bit_Switch jcs1_16bit_switch_2 (.I(INSTRUCTION[15:0]), .Activate(or_1_out), .R0(INSTR_ADDR));
  and and_14 (IS_OCLK, INSTRUCTION[23], not_20_out, INSTRUCTION[21], INSTRUCTION[20], INSTRUCTION[19]);
  and and_15 (IS_HALT, INSTRUCTION[23], INSTRUCTION[22], INSTRUCTION[21], INSTRUCTION[20], INSTRUCTION[19]);
  JCS1_16bit_Switch jcs1_16bit_switch_3 (.I(INSTRUCTION[15:0]), .Activate(or_2_out), .R0(RAM_ADDR));
  JC16_3bit_Reg_Switch jc16_3bit_reg_switch_3 (.I(INSTRUCTION[15:13]), .Activate(or_3_out), .R(PIN_ID_REG));
  Multiplexer #(.width(8)) multiplexer_1 (
    .in0({8{1'b0}}), .in1(INSTRUCTION[7:0]), .out(ALU_INSTR_BODY), .sel(not_1_out));
  Multiplexer #(.width(2)) multiplexer_2 (.in0(2'b00), .in1(INSTRUCTION[9:8]), .out(ALU_FLAG), .sel(not_1_out));

  assign REG_DEST = INSTRUCTION[18:16];
endmodule

module JCS1_32bit_Switch (
  input  [31:0] I,
  input  Activate,
  output [31:0] R0
);

  JCS1_16bit_Switch jcs1_16bit_switch_1 (.I(I[15:0]), .Activate(Activate), .R0(R0[15:0]));
  JCS1_16bit_Switch jcs1_16bit_switch_2 (.I(I[31:16]), .Activate(Activate), .R0(R0[31:16]));
endmodule

module JC16_16bit_RShift (
  input  [15:0] A,
  input  [15:0] B,
  output [15:0] R
);

  wire jc16_16bit_rshift_selector_1_wascarry, jc16_16bit_rshift_selector_2_wascarry,
       jc16_16bit_rshift_selector_3_wascarry, jc16_16bit_rshift_selector_4_wascarry,
       jc16_16bit_rshift_selector_5_wascarry, jc16_16bit_rshift_selector_6_wascarry,
       jc16_16bit_rshift_selector_7_wascarry, jc16_16bit_rshift_selector_8_wascarry,
       jc16_16bit_rshift_selector_9_wascarry, jc16_16bit_rshift_selector_10_wascarry,
       jc16_16bit_rshift_selector_11_wascarry, jc16_16bit_rshift_selector_12_wascarry,
       jc16_16bit_rshift_selector_13_wascarry, jc16_16bit_rshift_selector_14_wascarry,
       jc16_16bit_rshift_selector_15_wascarry, or_1_out;
  wire [3:0] jc16_16bit_rshift_selector_1_nextshiftby, jc16_16bit_rshift_selector_2_nextshiftby,
       jc16_16bit_rshift_selector_3_nextshiftby, jc16_16bit_rshift_selector_4_nextshiftby,
       jc16_16bit_rshift_selector_5_nextshiftby, jc16_16bit_rshift_selector_6_nextshiftby,
       jc16_16bit_rshift_selector_7_nextshiftby, jc16_16bit_rshift_selector_8_nextshiftby,
       jc16_16bit_rshift_selector_9_nextshiftby, jc16_16bit_rshift_selector_10_nextshiftby,
       jc16_16bit_rshift_selector_11_nextshiftby, jc16_16bit_rshift_selector_12_nextshiftby,
       jc16_16bit_rshift_selector_13_nextshiftby, jc16_16bit_rshift_selector_14_nextshiftby,
       jc16_16bit_rshift_selector_15_nextshiftby, jc16_16bit_rshift_selector_16_nextshiftby,
       multiplexer_1_out;

  Multiplexer #(.width(4)) multiplexer_1 (.in0(B[3:0]), .in1(4'b1111), .out(multiplexer_1_out), .sel(or_1_out));
  or or_1 (or_1_out, B[4], B[5], B[6], B[7], B[8], B[9], B[10], B[11], B[12], B[13], B[14], B[15]);
  JC16_16bit_RShift_selector jc16_16bit_rshift_selector_1 (
    .Num(A), .CarryIn(or_1_out), .ShiftBy(multiplexer_1_out), .Bit(R[0]),
    .NextShiftBy(jc16_16bit_rshift_selector_1_nextshiftby), .WasCarry(jc16_16bit_rshift_selector_1_wascarry));
  JC16_16bit_RShift_selector jc16_16bit_rshift_selector_2 (
    .Num(A), .CarryIn(jc16_16bit_rshift_selector_1_wascarry),
    .ShiftBy(jc16_16bit_rshift_selector_1_nextshiftby), .Bit(R[1]),
    .NextShiftBy(jc16_16bit_rshift_selector_2_nextshiftby), .WasCarry(jc16_16bit_rshift_selector_2_wascarry));
  JC16_16bit_RShift_selector jc16_16bit_rshift_selector_3 (
    .Num(A), .CarryIn(jc16_16bit_rshift_selector_2_wascarry),
    .ShiftBy(jc16_16bit_rshift_selector_2_nextshiftby), .Bit(R[2]),
    .NextShiftBy(jc16_16bit_rshift_selector_3_nextshiftby), .WasCarry(jc16_16bit_rshift_selector_3_wascarry));
  JC16_16bit_RShift_selector jc16_16bit_rshift_selector_4 (
    .Num(A), .CarryIn(jc16_16bit_rshift_selector_3_wascarry),
    .ShiftBy(jc16_16bit_rshift_selector_3_nextshiftby), .Bit(R[3]),
    .NextShiftBy(jc16_16bit_rshift_selector_4_nextshiftby), .WasCarry(jc16_16bit_rshift_selector_4_wascarry));
  JC16_16bit_RShift_selector jc16_16bit_rshift_selector_5 (
    .Num(A), .CarryIn(jc16_16bit_rshift_selector_4_wascarry),
    .ShiftBy(jc16_16bit_rshift_selector_4_nextshiftby), .Bit(R[4]),
    .NextShiftBy(jc16_16bit_rshift_selector_5_nextshiftby), .WasCarry(jc16_16bit_rshift_selector_5_wascarry));
  JC16_16bit_RShift_selector jc16_16bit_rshift_selector_6 (
    .Num(A), .CarryIn(jc16_16bit_rshift_selector_5_wascarry),
    .ShiftBy(jc16_16bit_rshift_selector_5_nextshiftby), .Bit(R[5]),
    .NextShiftBy(jc16_16bit_rshift_selector_6_nextshiftby), .WasCarry(jc16_16bit_rshift_selector_6_wascarry));
  JC16_16bit_RShift_selector jc16_16bit_rshift_selector_7 (
    .Num(A), .CarryIn(jc16_16bit_rshift_selector_6_wascarry),
    .ShiftBy(jc16_16bit_rshift_selector_6_nextshiftby), .Bit(R[6]),
    .NextShiftBy(jc16_16bit_rshift_selector_7_nextshiftby), .WasCarry(jc16_16bit_rshift_selector_7_wascarry));
  JC16_16bit_RShift_selector jc16_16bit_rshift_selector_8 (
    .Num(A), .CarryIn(jc16_16bit_rshift_selector_7_wascarry),
    .ShiftBy(jc16_16bit_rshift_selector_7_nextshiftby), .Bit(R[7]),
    .NextShiftBy(jc16_16bit_rshift_selector_8_nextshiftby), .WasCarry(jc16_16bit_rshift_selector_8_wascarry));
  JC16_16bit_RShift_selector jc16_16bit_rshift_selector_9 (
    .Num(A), .CarryIn(jc16_16bit_rshift_selector_8_wascarry),
    .ShiftBy(jc16_16bit_rshift_selector_8_nextshiftby), .Bit(R[8]),
    .NextShiftBy(jc16_16bit_rshift_selector_9_nextshiftby), .WasCarry(jc16_16bit_rshift_selector_9_wascarry));
  JC16_16bit_RShift_selector jc16_16bit_rshift_selector_10 (
    .Num(A), .CarryIn(jc16_16bit_rshift_selector_9_wascarry),
    .ShiftBy(jc16_16bit_rshift_selector_9_nextshiftby), .Bit(R[9]),
    .NextShiftBy(jc16_16bit_rshift_selector_10_nextshiftby), .WasCarry(jc16_16bit_rshift_selector_10_wascarry));
  JC16_16bit_RShift_selector jc16_16bit_rshift_selector_11 (
    .Num(A), .CarryIn(jc16_16bit_rshift_selector_10_wascarry),
    .ShiftBy(jc16_16bit_rshift_selector_10_nextshiftby), .Bit(R[10]),
    .NextShiftBy(jc16_16bit_rshift_selector_11_nextshiftby), .WasCarry(jc16_16bit_rshift_selector_11_wascarry));
  JC16_16bit_RShift_selector jc16_16bit_rshift_selector_12 (
    .Num(A), .CarryIn(jc16_16bit_rshift_selector_11_wascarry),
    .ShiftBy(jc16_16bit_rshift_selector_11_nextshiftby), .Bit(R[11]),
    .NextShiftBy(jc16_16bit_rshift_selector_12_nextshiftby), .WasCarry(jc16_16bit_rshift_selector_12_wascarry));
  JC16_16bit_RShift_selector jc16_16bit_rshift_selector_13 (
    .Num(A), .CarryIn(jc16_16bit_rshift_selector_12_wascarry),
    .ShiftBy(jc16_16bit_rshift_selector_12_nextshiftby), .Bit(R[12]),
    .NextShiftBy(jc16_16bit_rshift_selector_13_nextshiftby), .WasCarry(jc16_16bit_rshift_selector_13_wascarry));
  JC16_16bit_RShift_selector jc16_16bit_rshift_selector_14 (
    .Num(A), .CarryIn(jc16_16bit_rshift_selector_13_wascarry),
    .ShiftBy(jc16_16bit_rshift_selector_13_nextshiftby), .Bit(R[13]),
    .NextShiftBy(jc16_16bit_rshift_selector_14_nextshiftby), .WasCarry(jc16_16bit_rshift_selector_14_wascarry));
  JC16_16bit_RShift_selector jc16_16bit_rshift_selector_15 (
    .Num(A), .CarryIn(jc16_16bit_rshift_selector_14_wascarry),
    .ShiftBy(jc16_16bit_rshift_selector_14_nextshiftby), .Bit(R[14]),
    .NextShiftBy(jc16_16bit_rshift_selector_15_nextshiftby), .WasCarry(jc16_16bit_rshift_selector_15_wascarry));
  JC16_16bit_RShift_selector jc16_16bit_rshift_selector_16 (
    .Num(A), .CarryIn(jc16_16bit_rshift_selector_15_wascarry),
    .ShiftBy(jc16_16bit_rshift_selector_15_nextshiftby), .Bit(R[15]),
    .NextShiftBy(jc16_16bit_rshift_selector_16_nextshiftby));  // open: WasCarry
endmodule

module JC16_16bit_RShift_selector (
  input  [15:0] Num,
  input  CarryIn,
  input  [3:0] ShiftBy,
  output Bit,
  output [3:0] NextShiftBy,
  output WasCarry
);

  wire bitselector_1_out, jc16_4bitadder_1_carryout;

  BitSelector #(.width(16)) bitselector_1 (.in(Num), .out(bitselector_1_out), .sel(ShiftBy));
  Multiplexer multiplexer_1 (.in0(bitselector_1_out), .in1(1'b0), .out(Bit), .sel(CarryIn));
  JC16_4bitAdder jc16_4bitadder_1 (.A(ShiftBy), .B(4'b0001), .R(NextShiftBy), .CarryOut(jc16_4bitadder_1_carryout));
  or or_1 (WasCarry, jc16_4bitadder_1_carryout, CarryIn);
endmodule

module JC16_4bitAdder (
  input  [3:0] A,
  input  [3:0] B,
  output [3:0] R,
  output CarryOut
);

  wire jcs1_fulladder_1_carryout, jcs1_fulladder_2_carryout, jcs1_fulladder_3_carryout;

  JCS1_FullAdder jcs1_fulladder_1 (
    .A(A[0]), .B(B[0]), .CarryIn(1'b0), .Sum(R[0]), .CarryOut(jcs1_fulladder_1_carryout));
  JCS1_FullAdder jcs1_fulladder_2 (
    .A(A[1]), .B(B[1]), .CarryIn(jcs1_fulladder_1_carryout), .Sum(R[1]), .CarryOut(jcs1_fulladder_2_carryout));
  JCS1_FullAdder jcs1_fulladder_3 (
    .A(A[2]), .B(B[2]), .CarryIn(jcs1_fulladder_2_carryout), .Sum(R[2]), .CarryOut(jcs1_fulladder_3_carryout));
  JCS1_FullAdder jcs1_fulladder_4 (
    .A(A[3]), .B(B[3]), .CarryIn(jcs1_fulladder_3_carryout), .Sum(R[3]), .CarryOut(CarryOut));
endmodule

module JC16_16bit_LShift_selector (
  input  [15:0] Num,
  input  CarryIn,
  input  [3:0] ShiftBy,
  output Bit,
  output [3:0] NextShiftBy,
  output WasCarry
);

  wire bitselector_1_out, jc16_4bitadder_1_carryout, jc16_4bitsubtractor_1_carryout;
  wire [3:0] jc16_4bitsubtractor_1_r;

  BitSelector #(.width(16)) bitselector_1 (.in(Num), .out(bitselector_1_out), .sel(jc16_4bitsubtractor_1_r));
  Multiplexer multiplexer_1 (.in0(bitselector_1_out), .in1(1'b0), .out(Bit), .sel(CarryIn));
  JC16_4bitSubtractor jc16_4bitsubtractor_1 (
    .A(4'b1111), .B(ShiftBy), .R(jc16_4bitsubtractor_1_r), .CarryOut(jc16_4bitsubtractor_1_carryout));
  or or_1 (WasCarry, jc16_4bitsubtractor_1_carryout, jc16_4bitadder_1_carryout, CarryIn);
  JC16_4bitAdder jc16_4bitadder_1 (.A(ShiftBy), .B(4'b0001), .R(NextShiftBy), .CarryOut(jc16_4bitadder_1_carryout));
endmodule

module JC16_4bitSubtractor (
  input  [3:0] A,
  input  [3:0] B,
  output [3:0] R,
  output CarryOut
);

  wire jcs1_fullsubtractor_1_borrowout, jcs1_fullsubtractor_2_borrowout, jcs1_fullsubtractor_3_borrowout;

  JCS1_FullSubtractor jcs1_fullsubtractor_1 (
    .A(A[0]), .B(B[0]), .BorrowIn(1'b0), .Diff(R[0]), .BorrowOut(jcs1_fullsubtractor_1_borrowout));
  JCS1_FullSubtractor jcs1_fullsubtractor_2 (
    .A(A[1]), .B(B[1]), .BorrowIn(jcs1_fullsubtractor_1_borrowout), .Diff(R[1]),
    .BorrowOut(jcs1_fullsubtractor_2_borrowout));
  JCS1_FullSubtractor jcs1_fullsubtractor_3 (
    .A(A[2]), .B(B[2]), .BorrowIn(jcs1_fullsubtractor_2_borrowout), .Diff(R[2]),
    .BorrowOut(jcs1_fullsubtractor_3_borrowout));
  JCS1_FullSubtractor jcs1_fullsubtractor_4 (
    .A(A[3]), .B(B[3]), .BorrowIn(jcs1_fullsubtractor_3_borrowout), .Diff(R[3]), .BorrowOut(CarryOut));
endmodule

module JC16_16bit_LShift (
  input  [15:0] A,
  input  [15:0] B,
  output [15:0] R
);

  wire jc16_16bit_lshift_selector_1_wascarry, jc16_16bit_lshift_selector_2_wascarry,
       jc16_16bit_lshift_selector_3_wascarry, jc16_16bit_lshift_selector_4_wascarry,
       jc16_16bit_lshift_selector_5_wascarry, jc16_16bit_lshift_selector_6_wascarry,
       jc16_16bit_lshift_selector_7_wascarry, jc16_16bit_lshift_selector_8_wascarry,
       jc16_16bit_lshift_selector_9_wascarry, jc16_16bit_lshift_selector_10_wascarry,
       jc16_16bit_lshift_selector_11_wascarry, jc16_16bit_lshift_selector_12_wascarry,
       jc16_16bit_lshift_selector_13_wascarry, jc16_16bit_lshift_selector_14_wascarry,
       jc16_16bit_lshift_selector_15_wascarry, or_1_out;
  wire [3:0] jc16_16bit_lshift_selector_1_nextshiftby, jc16_16bit_lshift_selector_2_nextshiftby,
       jc16_16bit_lshift_selector_3_nextshiftby, jc16_16bit_lshift_selector_4_nextshiftby,
       jc16_16bit_lshift_selector_5_nextshiftby, jc16_16bit_lshift_selector_6_nextshiftby,
       jc16_16bit_lshift_selector_7_nextshiftby, jc16_16bit_lshift_selector_8_nextshiftby,
       jc16_16bit_lshift_selector_9_nextshiftby, jc16_16bit_lshift_selector_10_nextshiftby,
       jc16_16bit_lshift_selector_11_nextshiftby, jc16_16bit_lshift_selector_12_nextshiftby,
       jc16_16bit_lshift_selector_13_nextshiftby, jc16_16bit_lshift_selector_14_nextshiftby,
       jc16_16bit_lshift_selector_15_nextshiftby, multiplexer_1_out;
  wire [15:0] jc16_16bit_lshift_selector_1_bit;

  Multiplexer #(.width(4)) multiplexer_1 (.in0(B[3:0]), .in1(4'b1111), .out(multiplexer_1_out), .sel(or_1_out));
  or or_1 (or_1_out, B[4], B[5], B[6], B[7], B[8], B[9], B[10], B[11], B[12], B[13], B[14], B[15]);
  JC16_16bit_LShift_selector jc16_16bit_lshift_selector_1 (
    .Num(A), .CarryIn(or_1_out), .ShiftBy(multiplexer_1_out), .Bit(jc16_16bit_lshift_selector_1_bit[0]),
    .NextShiftBy(jc16_16bit_lshift_selector_1_nextshiftby), .WasCarry(jc16_16bit_lshift_selector_1_wascarry));
  JC16_16bit_LShift_selector jc16_16bit_lshift_selector_2 (
    .Num(A), .CarryIn(jc16_16bit_lshift_selector_1_wascarry),
    .ShiftBy(jc16_16bit_lshift_selector_1_nextshiftby), .Bit(jc16_16bit_lshift_selector_1_bit[1]),
    .NextShiftBy(jc16_16bit_lshift_selector_2_nextshiftby), .WasCarry(jc16_16bit_lshift_selector_2_wascarry));
  JC16_16bit_LShift_selector jc16_16bit_lshift_selector_3 (
    .Num(A), .CarryIn(jc16_16bit_lshift_selector_2_wascarry),
    .ShiftBy(jc16_16bit_lshift_selector_2_nextshiftby), .Bit(jc16_16bit_lshift_selector_1_bit[2]),
    .NextShiftBy(jc16_16bit_lshift_selector_3_nextshiftby), .WasCarry(jc16_16bit_lshift_selector_3_wascarry));
  JC16_16bit_LShift_selector jc16_16bit_lshift_selector_4 (
    .Num(A), .CarryIn(jc16_16bit_lshift_selector_3_wascarry),
    .ShiftBy(jc16_16bit_lshift_selector_3_nextshiftby), .Bit(jc16_16bit_lshift_selector_1_bit[3]),
    .NextShiftBy(jc16_16bit_lshift_selector_4_nextshiftby), .WasCarry(jc16_16bit_lshift_selector_4_wascarry));
  JC16_16bit_LShift_selector jc16_16bit_lshift_selector_5 (
    .Num(A), .CarryIn(jc16_16bit_lshift_selector_4_wascarry),
    .ShiftBy(jc16_16bit_lshift_selector_4_nextshiftby), .Bit(jc16_16bit_lshift_selector_1_bit[4]),
    .NextShiftBy(jc16_16bit_lshift_selector_5_nextshiftby), .WasCarry(jc16_16bit_lshift_selector_5_wascarry));
  JC16_16bit_LShift_selector jc16_16bit_lshift_selector_6 (
    .Num(A), .CarryIn(jc16_16bit_lshift_selector_5_wascarry),
    .ShiftBy(jc16_16bit_lshift_selector_5_nextshiftby), .Bit(jc16_16bit_lshift_selector_1_bit[5]),
    .NextShiftBy(jc16_16bit_lshift_selector_6_nextshiftby), .WasCarry(jc16_16bit_lshift_selector_6_wascarry));
  JC16_16bit_LShift_selector jc16_16bit_lshift_selector_7 (
    .Num(A), .CarryIn(jc16_16bit_lshift_selector_6_wascarry),
    .ShiftBy(jc16_16bit_lshift_selector_6_nextshiftby), .Bit(jc16_16bit_lshift_selector_1_bit[6]),
    .NextShiftBy(jc16_16bit_lshift_selector_7_nextshiftby), .WasCarry(jc16_16bit_lshift_selector_7_wascarry));
  JC16_16bit_LShift_selector jc16_16bit_lshift_selector_8 (
    .Num(A), .CarryIn(jc16_16bit_lshift_selector_7_wascarry),
    .ShiftBy(jc16_16bit_lshift_selector_7_nextshiftby), .Bit(jc16_16bit_lshift_selector_1_bit[7]),
    .NextShiftBy(jc16_16bit_lshift_selector_8_nextshiftby), .WasCarry(jc16_16bit_lshift_selector_8_wascarry));
  JC16_16bit_LShift_selector jc16_16bit_lshift_selector_9 (
    .Num(A), .CarryIn(jc16_16bit_lshift_selector_8_wascarry),
    .ShiftBy(jc16_16bit_lshift_selector_8_nextshiftby), .Bit(jc16_16bit_lshift_selector_1_bit[8]),
    .NextShiftBy(jc16_16bit_lshift_selector_9_nextshiftby), .WasCarry(jc16_16bit_lshift_selector_9_wascarry));
  JC16_16bit_LShift_selector jc16_16bit_lshift_selector_10 (
    .Num(A), .CarryIn(jc16_16bit_lshift_selector_9_wascarry),
    .ShiftBy(jc16_16bit_lshift_selector_9_nextshiftby), .Bit(jc16_16bit_lshift_selector_1_bit[9]),
    .NextShiftBy(jc16_16bit_lshift_selector_10_nextshiftby), .WasCarry(jc16_16bit_lshift_selector_10_wascarry));
  JC16_16bit_LShift_selector jc16_16bit_lshift_selector_11 (
    .Num(A), .CarryIn(jc16_16bit_lshift_selector_10_wascarry),
    .ShiftBy(jc16_16bit_lshift_selector_10_nextshiftby), .Bit(jc16_16bit_lshift_selector_1_bit[10]),
    .NextShiftBy(jc16_16bit_lshift_selector_11_nextshiftby), .WasCarry(jc16_16bit_lshift_selector_11_wascarry));
  JC16_16bit_LShift_selector jc16_16bit_lshift_selector_12 (
    .Num(A), .CarryIn(jc16_16bit_lshift_selector_11_wascarry),
    .ShiftBy(jc16_16bit_lshift_selector_11_nextshiftby), .Bit(jc16_16bit_lshift_selector_1_bit[11]),
    .NextShiftBy(jc16_16bit_lshift_selector_12_nextshiftby), .WasCarry(jc16_16bit_lshift_selector_12_wascarry));
  JC16_16bit_LShift_selector jc16_16bit_lshift_selector_13 (
    .Num(A), .CarryIn(jc16_16bit_lshift_selector_12_wascarry),
    .ShiftBy(jc16_16bit_lshift_selector_12_nextshiftby), .Bit(jc16_16bit_lshift_selector_1_bit[12]),
    .NextShiftBy(jc16_16bit_lshift_selector_13_nextshiftby), .WasCarry(jc16_16bit_lshift_selector_13_wascarry));
  JC16_16bit_LShift_selector jc16_16bit_lshift_selector_14 (
    .Num(A), .CarryIn(jc16_16bit_lshift_selector_13_wascarry),
    .ShiftBy(jc16_16bit_lshift_selector_13_nextshiftby), .Bit(jc16_16bit_lshift_selector_1_bit[13]),
    .NextShiftBy(jc16_16bit_lshift_selector_14_nextshiftby), .WasCarry(jc16_16bit_lshift_selector_14_wascarry));
  JC16_16bit_LShift_selector jc16_16bit_lshift_selector_15 (
    .Num(A), .CarryIn(jc16_16bit_lshift_selector_14_wascarry),
    .ShiftBy(jc16_16bit_lshift_selector_14_nextshiftby), .Bit(jc16_16bit_lshift_selector_1_bit[14]),
    .NextShiftBy(jc16_16bit_lshift_selector_15_nextshiftby), .WasCarry(jc16_16bit_lshift_selector_15_wascarry));
  JC16_16bit_LShift_selector jc16_16bit_lshift_selector_16 (
    .Num(A), .CarryIn(jc16_16bit_lshift_selector_15_wascarry),
    .ShiftBy(jc16_16bit_lshift_selector_15_nextshiftby), .Bit(jc16_16bit_lshift_selector_1_bit[15]));  // open: NextShiftBy, WasCarry
  JC16_16bit_Reverse jc16_16bit_reverse_1 (.A(jc16_16bit_lshift_selector_1_bit), .R(R));
endmodule

module JC16_16bit_Reverse (
  input  [15:0] A,
  output [15:0] R
);


  assign R = {A[0], A[1], A[2], A[3], A[4], A[5], A[6], A[7], A[8], A[9], A[10], A[11], A[12], A[13], A[14], A[15]};
endmodule

module JC16_16bit_Equal (
  input  [15:0] A,
  input  [15:0] B,
  output [15:0] R
);

  wire or_1_out;
  wire [15:0] jcs1_16bit_xor_1_r;

  JCS1_16bit_XOR jcs1_16bit_xor_1 (.A(A), .B(B), .R(jcs1_16bit_xor_1_r));
  or or_1 (or_1_out, jcs1_16bit_xor_1_r[0], jcs1_16bit_xor_1_r[1], jcs1_16bit_xor_1_r[2], jcs1_16bit_xor_1_r[3], jcs1_16bit_xor_1_r[4], jcs1_16bit_xor_1_r[5], jcs1_16bit_xor_1_r[6], jcs1_16bit_xor_1_r[7], jcs1_16bit_xor_1_r[8], jcs1_16bit_xor_1_r[9], jcs1_16bit_xor_1_r[10], jcs1_16bit_xor_1_r[11], jcs1_16bit_xor_1_r[12], jcs1_16bit_xor_1_r[13], jcs1_16bit_xor_1_r[14], jcs1_16bit_xor_1_r[15]);
  not not_1 (R[0], or_1_out);

  assign R[15:1] = {15{1'b0}};
endmodule

module JC16_16bit_GreaterThan (
  input  [15:0] A,
  input  [15:0] B,
  output [15:0] R
);

  wire jc16_1bit_agtb_1_godeeper, jc16_1bit_agtb_1_r, jc16_1bit_agtb_2_godeeper, jc16_1bit_agtb_2_r,
       jc16_1bit_agtb_3_godeeper, jc16_1bit_agtb_3_r, jc16_1bit_agtb_4_godeeper, jc16_1bit_agtb_4_r,
       jc16_1bit_agtb_5_godeeper, jc16_1bit_agtb_5_r, jc16_1bit_agtb_6_godeeper, jc16_1bit_agtb_6_r,
       jc16_1bit_agtb_7_godeeper, jc16_1bit_agtb_7_r, jc16_1bit_agtb_8_godeeper, jc16_1bit_agtb_8_r,
       jc16_1bit_agtb_9_godeeper, jc16_1bit_agtb_9_r, jc16_1bit_agtb_10_godeeper, jc16_1bit_agtb_10_r,
       jc16_1bit_agtb_11_godeeper, jc16_1bit_agtb_11_r, jc16_1bit_agtb_12_godeeper, jc16_1bit_agtb_12_r,
       jc16_1bit_agtb_13_godeeper, jc16_1bit_agtb_13_r, jc16_1bit_agtb_14_godeeper, jc16_1bit_agtb_14_r,
       jc16_1bit_agtb_15_godeeper, jc16_1bit_agtb_15_r, jc16_1bit_agtb_16_r;

  JC16_1bit_AgtB jc16_1bit_agtb_1 (
    .Check(1'b1), .A(A[15]), .B(B[15]), .R(jc16_1bit_agtb_1_r), .GoDeeper(jc16_1bit_agtb_1_godeeper));
  JC16_1bit_AgtB jc16_1bit_agtb_2 (
    .Check(jc16_1bit_agtb_1_godeeper), .A(A[14]), .B(B[14]), .R(jc16_1bit_agtb_2_r),
    .GoDeeper(jc16_1bit_agtb_2_godeeper));
  JC16_1bit_AgtB jc16_1bit_agtb_3 (
    .Check(jc16_1bit_agtb_2_godeeper), .A(A[13]), .B(B[13]), .R(jc16_1bit_agtb_3_r),
    .GoDeeper(jc16_1bit_agtb_3_godeeper));
  JC16_1bit_AgtB jc16_1bit_agtb_4 (
    .Check(jc16_1bit_agtb_3_godeeper), .A(A[12]), .B(B[12]), .R(jc16_1bit_agtb_4_r),
    .GoDeeper(jc16_1bit_agtb_4_godeeper));
  JC16_1bit_AgtB jc16_1bit_agtb_5 (
    .Check(jc16_1bit_agtb_4_godeeper), .A(A[11]), .B(B[11]), .R(jc16_1bit_agtb_5_r),
    .GoDeeper(jc16_1bit_agtb_5_godeeper));
  JC16_1bit_AgtB jc16_1bit_agtb_6 (
    .Check(jc16_1bit_agtb_5_godeeper), .A(A[10]), .B(B[10]), .R(jc16_1bit_agtb_6_r),
    .GoDeeper(jc16_1bit_agtb_6_godeeper));
  JC16_1bit_AgtB jc16_1bit_agtb_7 (
    .Check(jc16_1bit_agtb_6_godeeper), .A(A[9]), .B(B[9]), .R(jc16_1bit_agtb_7_r),
    .GoDeeper(jc16_1bit_agtb_7_godeeper));
  JC16_1bit_AgtB jc16_1bit_agtb_8 (
    .Check(jc16_1bit_agtb_7_godeeper), .A(A[8]), .B(B[8]), .R(jc16_1bit_agtb_8_r),
    .GoDeeper(jc16_1bit_agtb_8_godeeper));
  JC16_1bit_AgtB jc16_1bit_agtb_9 (
    .Check(jc16_1bit_agtb_8_godeeper), .A(A[7]), .B(B[7]), .R(jc16_1bit_agtb_9_r),
    .GoDeeper(jc16_1bit_agtb_9_godeeper));
  JC16_1bit_AgtB jc16_1bit_agtb_10 (
    .Check(jc16_1bit_agtb_9_godeeper), .A(A[6]), .B(B[6]), .R(jc16_1bit_agtb_10_r),
    .GoDeeper(jc16_1bit_agtb_10_godeeper));
  JC16_1bit_AgtB jc16_1bit_agtb_11 (
    .Check(jc16_1bit_agtb_10_godeeper), .A(A[5]), .B(B[5]), .R(jc16_1bit_agtb_11_r),
    .GoDeeper(jc16_1bit_agtb_11_godeeper));
  JC16_1bit_AgtB jc16_1bit_agtb_12 (
    .Check(jc16_1bit_agtb_11_godeeper), .A(A[4]), .B(B[4]), .R(jc16_1bit_agtb_12_r),
    .GoDeeper(jc16_1bit_agtb_12_godeeper));
  JC16_1bit_AgtB jc16_1bit_agtb_13 (
    .Check(jc16_1bit_agtb_12_godeeper), .A(A[3]), .B(B[3]), .R(jc16_1bit_agtb_13_r),
    .GoDeeper(jc16_1bit_agtb_13_godeeper));
  JC16_1bit_AgtB jc16_1bit_agtb_14 (
    .Check(jc16_1bit_agtb_13_godeeper), .A(A[2]), .B(B[2]), .R(jc16_1bit_agtb_14_r),
    .GoDeeper(jc16_1bit_agtb_14_godeeper));
  JC16_1bit_AgtB jc16_1bit_agtb_15 (
    .Check(jc16_1bit_agtb_14_godeeper), .A(A[1]), .B(B[1]), .R(jc16_1bit_agtb_15_r),
    .GoDeeper(jc16_1bit_agtb_15_godeeper));
  JC16_1bit_AgtB jc16_1bit_agtb_16 (
    .Check(jc16_1bit_agtb_15_godeeper), .A(A[0]), .B(B[0]), .R(jc16_1bit_agtb_16_r));  // open: GoDeeper
  or or_1 (R[0], jc16_1bit_agtb_1_r, jc16_1bit_agtb_2_r, jc16_1bit_agtb_3_r, jc16_1bit_agtb_4_r, jc16_1bit_agtb_5_r, jc16_1bit_agtb_6_r, jc16_1bit_agtb_7_r, jc16_1bit_agtb_8_r, jc16_1bit_agtb_9_r, jc16_1bit_agtb_10_r, jc16_1bit_agtb_11_r, jc16_1bit_agtb_12_r, jc16_1bit_agtb_13_r, jc16_1bit_agtb_14_r, jc16_1bit_agtb_15_r, jc16_1bit_agtb_16_r);

  assign R[15:1] = {15{1'b0}};
endmodule

module JC16_1bit_AgtB (
  input  Check,
  input  A,
  input  B,
  output R,
  output GoDeeper
);

  wire not_1_out, not_2_out, xor_1_out;

  and and_1 (R, A, Check, not_1_out);
  not not_1 (not_1_out, B);
  xor xor_1 (xor_1_out, A, B);
  not not_2 (not_2_out, xor_1_out);
  and and_2 (GoDeeper, not_2_out, Check);
endmodule

module JC16_16bit_LessThan (
  input  [15:0] A,
  input  [15:0] B,
  output [15:0] R
);

  wire not_1_out, not_2_out;
  wire [15:0] jc16_16bit_equal_1_r, jc16_16bit_greaterthan_1_r;

  JC16_16bit_GreaterThan jc16_16bit_greaterthan_1 (.A(A), .B(B), .R(jc16_16bit_greaterthan_1_r));
  JC16_16bit_Equal jc16_16bit_equal_1 (.A(A), .B(B), .R(jc16_16bit_equal_1_r));
  not not_1 (not_1_out, jc16_16bit_greaterthan_1_r[0]);
  not not_2 (not_2_out, jc16_16bit_equal_1_r[0]);
  and and_1 (R[0], not_1_out, not_2_out);

  assign R[15:1] = {15{1'b0}};
endmodule

module JC16_CPU (
  input  CLK,
  input  [23:0] INSTRUCTION,
  input  [23:0] SECOND_INSTR,
  input  [15:0] RAM_VAL_LD,
  input  [15:0] I_PIN0,
  input  [15:0] I_PIN1,
  input  [15:0] I_PIN2,
  input  [15:0] I_PIN3,
  output [15:0] RAM_ADDR,
  output [15:0] ROM_ADDR,
  output LDRAM,
  output OCLK,
  output RUN_CLK,
  output STRAM,
  output [15:0] RAM_VAL_ST,
  output [15:0] O_PIN0,
  output [15:0] O_PIN1,
  output [15:0] O_PIN2,
  output [15:0] O_PIN3
);

  wire alu_c, ALU_CARRY_P, alu_nc, alu_nz, alu_z, and_2_out, and_3_out, and_4_out, and_5_out, d_ff_1_q,
       demultiplexer_2_out0, demultiplexer_2_out1, demultiplexer_2_out2, demultiplexer_2_out3, IS_PARALLEL,
       jc16_tiny_instruction_decoder_1_is_alu, jcs1_alu_2_carry, jcs1_instruction_decoder_1_is_alu,
       jcs1_instruction_decoder_1_is_halt, jcs1_instruction_decoder_1_is_jic,
       jcs1_instruction_decoder_1_is_jiz, jcs1_instruction_decoder_1_is_jmp,
       jcs1_instruction_decoder_1_is_jnc, jcs1_instruction_decoder_1_is_jnz,
       jcs1_instruction_decoder_1_is_ldi, jcs1_instruction_decoder_1_is_rdpin,
       jcs1_instruction_decoder_1_is_wrpin, multiplexer_6_out, nor_1_out, not_2_out, not_3_out, or_1_out,
       or_2_out, or_3_out, register_6_q, WRITE_P;
  wire [1:0] ALU_FLAG, jc16_tiny_instruction_decoder_1_flag;
  wire [2:0] ALU_reg_a, ALU_reg_b, jc16_tiny_instruction_decoder_1_reg_a,
       jc16_tiny_instruction_decoder_1_reg_b, jcs1_instruction_decoder_1_reg_dest, pin_id_reg,
       priority_encoder_1_out, R_ID_P, regid_dest_wrpin;
  wire [3:0] ALU_instr, jc16_tiny_instruction_decoder_1_alu_f;
  wire [7:0] ALU_BODY, jc16_tiny_instruction_decoder_1_alu_body;
  wire [15:0] demultiplexer_1_out0, demultiplexer_1_out1, demultiplexer_1_out2, demultiplexer_1_out3, INP_P,
       jc16_alu_input_handler_1_o_a, jc16_alu_input_handler_1_o_b, jc16_alu_input_handler_2_o_a,
       jc16_alu_input_handler_2_o_b, jcs1_alu_2_r, jcs1_instruction_decoder_1_instr_addr,
       jcs1_instruction_decoder_1_ldi_value, jcs1_instruction_decoder_1_ram_addr, jcs1_program_counter_1_pr,
       multiplexer_1_out, multiplexer_2_out, multiplexer_4_out, multiplexer_5_out, r0, r1, r2, r3, r4, r5,
       r6, r7, RAM_SHIFT_q, rdpin_val, register_5_q, ROM_SHIFT_q;

  Register #(.width(16)) ROM_SHIFT (.D({16{1'b0}}), .Q(ROM_SHIFT_q));  // open: en, clk, clr
  JCS1_Program_Counter jcs1_program_counter_1 (
    .CLK(CLK), .WR(or_1_out), .V(jcs1_instruction_decoder_1_instr_addr), .WAS_PARALLEL(IS_PARALLEL),
    .PR(jcs1_program_counter_1_pr));
  Adder #(.width(16)) adder_1 (.a(jcs1_program_counter_1_pr), .b(ROM_SHIFT_q), .out(ROM_ADDR));  // open: cin, cout
  or or_1 (or_1_out, jcs1_instruction_decoder_1_is_jmp, and_2_out, and_3_out, and_4_out, and_5_out);
  and and_1 (WRITE_P, IS_PARALLEL, jc16_tiny_instruction_decoder_1_is_alu);
  JC16_Tiny_Instruction_Decoder jc16_tiny_instruction_decoder_1 (
    .INSTR(SECOND_INSTR), .IS_ALU(jc16_tiny_instruction_decoder_1_is_alu),
    .ALU_F(jc16_tiny_instruction_decoder_1_alu_f), .TARGET_REG(R_ID_P),
    .REG_A(jc16_tiny_instruction_decoder_1_reg_a), .REG_B(jc16_tiny_instruction_decoder_1_reg_b),
    .FLAG(jc16_tiny_instruction_decoder_1_flag), .ALU_BODY(jc16_tiny_instruction_decoder_1_alu_body));
  JC16_ALU_Input_Handler jc16_alu_input_handler_1 (
    .FLAG(jc16_tiny_instruction_decoder_1_flag), .ELABORATE_BODY(jc16_tiny_instruction_decoder_1_alu_body),
    .I_R0(r0), .I_R1(r1), .I_R2(r2), .I_R3(r3), .I_R4(r4), .I_R5(r5), .I_R6(r6), .I_R7(r7),
    .REG_A(jc16_tiny_instruction_decoder_1_reg_a), .REG_B(jc16_tiny_instruction_decoder_1_reg_b),
    .O_A(jc16_alu_input_handler_1_o_a), .O_B(jc16_alu_input_handler_1_o_b));
  and and_2 (and_2_out, jcs1_instruction_decoder_1_is_jiz, alu_z);
  and and_3 (and_3_out, jcs1_instruction_decoder_1_is_jnz, alu_nz);
  and and_4 (and_4_out, jcs1_instruction_decoder_1_is_jic, alu_c);
  and and_5 (and_5_out, jcs1_instruction_decoder_1_is_jnc, alu_nc);
  JCS1_ALU jcs1_alu_1 (
    .F(jc16_tiny_instruction_decoder_1_alu_f), .A(jc16_alu_input_handler_1_o_a),
    .B(jc16_alu_input_handler_1_o_b), .R(INP_P), .Carry(ALU_CARRY_P));
  Multiplexer #(.select(3), .width(16)) multiplexer_1 (
    .in0(r0), .in1(r1), .in2(r2), .in3(r3), .in4(r4), .in5(r5), .in6(r6), .in7(r7), .out(multiplexer_1_out),
    .sel(pin_id_reg));
  JCS1_Instruction_Decoder jcs1_instruction_decoder_1 (
    .INSTRUCTION(INSTRUCTION), .REG_DEST(jcs1_instruction_decoder_1_reg_dest),
    .IS_ALU(jcs1_instruction_decoder_1_is_alu), .ALU_REG_A(ALU_reg_a), .ALU_REG_B(ALU_reg_b),
    .ALU_INSTR(ALU_instr), .IS_LDI(jcs1_instruction_decoder_1_is_ldi),
    .LDI_VALUE(jcs1_instruction_decoder_1_ldi_value), .IS_JMP(jcs1_instruction_decoder_1_is_jmp),
    .IS_JIZ(jcs1_instruction_decoder_1_is_jiz), .IS_JNZ(jcs1_instruction_decoder_1_is_jnz),
    .IS_JIC(jcs1_instruction_decoder_1_is_jic), .IS_JNC(jcs1_instruction_decoder_1_is_jnc),
    .INSTR_ADDR(jcs1_instruction_decoder_1_instr_addr), .IS_OCLK(OCLK),
    .IS_HALT(jcs1_instruction_decoder_1_is_halt), .IS_LDRAM(LDRAM), .IS_STRAM(STRAM),
    .RAM_ADDR(jcs1_instruction_decoder_1_ram_addr), .IS_RDPIN(jcs1_instruction_decoder_1_is_rdpin),
    .IS_WRPIN(jcs1_instruction_decoder_1_is_wrpin), .PIN_ID_REG(pin_id_reg), .ALU_INSTR_BODY(ALU_BODY),
    .ALU_FLAG(ALU_FLAG));
  D_Flip_Flop d_ff_1 (
    .D(jcs1_instruction_decoder_1_is_halt), .clk(jcs1_instruction_decoder_1_is_halt), .Q(d_ff_1_q),
    .reset(LDRAM));  // open: Qn, preset
  JC16_Parallelism_Detection jc16_parallelism_detection_1 (
    .INSTR_A(INSTRUCTION), .INSTR_B(SECOND_INSTR), .CAN_RUN_PARALLEL(IS_PARALLEL));
  Multiplexer #(.select(3), .width(16)) multiplexer_2 (
    .in0(r0), .in1(r1), .in2(r2), .in3(r3), .in4(r4), .in5(r5), .in6(r6), .in7(r7), .out(multiplexer_2_out),
    .sel(regid_dest_wrpin));
  Register #(.width(16)) RAM_SHIFT (.D({16{1'b0}}), .Q(RAM_SHIFT_q));  // open: en, clk, clr
  not not_1 (RUN_CLK, d_ff_1_q);
  JC16_ALU_Input_Handler jc16_alu_input_handler_2 (
    .FLAG(ALU_FLAG), .ELABORATE_BODY(ALU_BODY), .I_R0(r0), .I_R1(r1), .I_R2(r2), .I_R3(r3), .I_R4(r4),
    .I_R5(r5), .I_R6(r6), .I_R7(r7), .REG_A(ALU_reg_a), .REG_B(ALU_reg_b),
    .O_A(jc16_alu_input_handler_2_o_a), .O_B(jc16_alu_input_handler_2_o_b));
  Multiplexer #(.select(2), .width(16)) multiplexer_3 (
    .in0(I_PIN0), .in1(I_PIN1), .in2(I_PIN2), .in3(I_PIN3), .out(rdpin_val), .sel(multiplexer_1_out[1:0]));
  or or_2 (or_2_out, jcs1_instruction_decoder_1_is_alu, LDRAM, jcs1_instruction_decoder_1_is_rdpin, jcs1_instruction_decoder_1_is_ldi);
  Adder #(.width(16)) adder_2 (
    .a(jcs1_instruction_decoder_1_ram_addr), .b(RAM_SHIFT_q), .out(RAM_ADDR));  // open: cin, cout
  Multiplexer #(.select(3), .width(16)) multiplexer_4 (
    .in0(jcs1_alu_2_r), .in1(jcs1_instruction_decoder_1_ldi_value), .in2(RAM_VAL_LD), .in3(rdpin_val),
    .out(multiplexer_4_out), .sel(priority_encoder_1_out));  // open: in4, in5, in6, in7
  Priority_Encoder priority_encoder_1 (
    .in0(jcs1_instruction_decoder_1_is_alu), .in1(jcs1_instruction_decoder_1_is_ldi), .in2(LDRAM),
    .in3(jcs1_instruction_decoder_1_is_rdpin), .out(priority_encoder_1_out));  // open: in4, in5, in6, in7, en_in, gs, en_out
  Demultiplexer #(.select(2), .width(16)) demultiplexer_1 (
    .out0(demultiplexer_1_out0), .out1(demultiplexer_1_out1), .out2(demultiplexer_1_out2),
    .out3(demultiplexer_1_out3), .in(multiplexer_2_out), .sel(multiplexer_1_out[1:0]));
  Demultiplexer #(.select(2)) demultiplexer_2 (
    .out0(demultiplexer_2_out0), .out1(demultiplexer_2_out1), .out2(demultiplexer_2_out2),
    .out3(demultiplexer_2_out3), .in(jcs1_instruction_decoder_1_is_wrpin), .sel(multiplexer_1_out[1:0]));
  assign regid_dest_wrpin = jcs1_instruction_decoder_1_reg_dest;  // Buffer buffer_1, 3 bits wide
  JCS1_ALU jcs1_alu_2 (
    .F(ALU_instr), .A(jc16_alu_input_handler_2_o_a), .B(jc16_alu_input_handler_2_o_b), .R(jcs1_alu_2_r),
    .Carry(jcs1_alu_2_carry));
  Multiplexer #(.width(16)) multiplexer_5 (.in0(jcs1_alu_2_r), .in1(INP_P), .out(multiplexer_5_out), .sel(IS_PARALLEL));
  or or_3 (or_3_out, jcs1_instruction_decoder_1_is_alu, IS_PARALLEL);
  Multiplexer multiplexer_6 (.in0(jcs1_alu_2_carry), .in1(ALU_CARRY_P), .out(multiplexer_6_out), .sel(IS_PARALLEL));
  Register #(.width(16)) register_1 (
    .D(demultiplexer_1_out0), .en(demultiplexer_2_out0), .clk(CLK), .Q(O_PIN0));  // open: clr
  Register #(.width(16)) register_2 (
    .D(demultiplexer_1_out1), .en(demultiplexer_2_out1), .clk(CLK), .Q(O_PIN1));  // open: clr
  Register #(.width(16)) register_3 (
    .D(demultiplexer_1_out2), .en(demultiplexer_2_out2), .clk(CLK), .Q(O_PIN2));  // open: clr
  Register #(.width(16)) register_4 (
    .D(demultiplexer_1_out3), .en(demultiplexer_2_out3), .clk(CLK), .Q(O_PIN3));  // open: clr
  JC16_Registers jc16_registers_1 (
    .CLK(CLK), .REG_ID(jcs1_instruction_decoder_1_reg_dest), .INP(multiplexer_4_out), .WRITE(or_2_out),
    .R_ID_P(R_ID_P), .INP_P(INP_P), .WRITE_P(WRITE_P), .R0(r0), .R1(r1), .R2(r2), .R3(r3), .R4(r4), .R5(r5),
    .R6(r6), .R7(r7));
  Register #(.width(16)) register_5 (.D(multiplexer_5_out), .en(or_3_out), .clk(CLK), .Q(register_5_q));  // open: clr
  Register #(.width(1)) register_6 (.D(multiplexer_6_out), .en(or_3_out), .clk(CLK), .Q(register_6_q));  // open: clr
  Multiplexer #(.select(3), .width(16)) multiplexer_7 (
    .in0(r0), .in1(r1), .in2(r2), .in3(r3), .in4(r4), .in5(r5), .in6(r6), .in7(r7), .out(RAM_VAL_ST),
    .sel(jcs1_instruction_decoder_1_reg_dest));
  not not_2 (not_2_out, register_6_q);
  buf buffer_2 (alu_nc, not_2_out);
  buf buffer_3 (alu_c, register_6_q);
  nor nor_1 (nor_1_out, register_5_q[15], register_5_q[14], register_5_q[13], register_5_q[12], register_5_q[11], register_5_q[10], register_5_q[9], register_5_q[8], register_5_q[6], register_5_q[5], register_5_q[4], register_5_q[3], register_5_q[2], register_5_q[1], register_5_q[0], register_5_q[7]);
  not not_3 (not_3_out, nor_1_out);
  buf buffer_4 (alu_nz, not_3_out);
  buf buffer_5 (alu_z, nor_1_out);
endmodule

module JC16_3bit_Reg_Switch (
  input  [2:0] I,
  input  Activate,
  output [2:0] R
);

  and and_1 (R[0], I[0], Activate);
  and and_2 (R[1], I[1], Activate);
  and and_3 (R[2], I[2], Activate);
endmodule

module JC16_4bit_Switch (
  input  [3:0] I,
  input  Activate,
  output [3:0] R
);

  and and_1 (R[0], I[0], Activate);
  and and_2 (R[1], I[1], Activate);
  and and_3 (R[2], I[2], Activate);
  and and_4 (R[3], I[3], Activate);
endmodule

module JC16_Registers (
  input  CLK,
  input  [2:0] REG_ID,
  input  [15:0] INP,
  input  WRITE,
  input  [2:0] R_ID_P,
  input  [15:0] INP_P,
  input  WRITE_P,
  output [15:0] R0,
  output [15:0] R1,
  output [15:0] R2,
  output [15:0] R3,
  output [15:0] R4,
  output [15:0] R5,
  output [15:0] R6,
  output [15:0] R7
);

  wire or_1_out, or_2_out, or_3_out, or_4_out, or_5_out, or_6_out, or_7_out, or_8_out, WE_P0, WE_P1, WE_P2,
       WE_P3, WE_P4, WE_P5, WE_P6, WE_P7, WE_S0, WE_S1, WE_S2, WE_S3, WE_S4, WE_S5, WE_S6, WE_S7;
  wire [15:0] I_P0, I_P1, I_P2, I_P3, I_P4, I_P5, I_P6, I_P7, I_S0, I_S1, I_S2, I_S3, I_S4, I_S5, I_S6, I_S7,
       multiplexer_1_out, multiplexer_2_out, multiplexer_3_out, multiplexer_4_out, multiplexer_5_out,
       multiplexer_6_out, multiplexer_7_out, multiplexer_8_out;

  Demultiplexer #(.select(3), .width(16)) demultiplexer_1 (
    .out0(I_S0), .out1(I_S1), .out2(I_S2), .out3(I_S3), .out4(I_S4), .out5(I_S5), .out6(I_S6), .out7(I_S7),
    .in(INP), .sel(REG_ID));
  Demultiplexer #(.select(3)) demultiplexer_2 (
    .out0(WE_S0), .out1(WE_S1), .out2(WE_S2), .out3(WE_S3), .out4(WE_S4), .out5(WE_S5), .out6(WE_S6),
    .out7(WE_S7), .in(WRITE), .sel(REG_ID));
  Demultiplexer #(.select(3), .width(16)) demultiplexer_3 (
    .out0(I_P0), .out1(I_P1), .out2(I_P2), .out3(I_P3), .out4(I_P4), .out5(I_P5), .out6(I_P6), .out7(I_P7),
    .in(INP_P), .sel(R_ID_P));
  Demultiplexer #(.select(3)) demultiplexer_4 (
    .out0(WE_P0), .out1(WE_P1), .out2(WE_P2), .out3(WE_P3), .out4(WE_P4), .out5(WE_P5), .out6(WE_P6),
    .out7(WE_P7), .in(WRITE_P), .sel(R_ID_P));
  Register #(.width(16)) register_1 (.D(multiplexer_1_out), .en(or_1_out), .clk(CLK), .Q(R0));  // open: clr
  Multiplexer #(.width(16)) multiplexer_1 (.in0(I_S0), .in1(I_P0), .out(multiplexer_1_out), .sel(WE_P0));
  or or_1 (or_1_out, WE_S0, WE_P0);
  Register #(.width(16)) register_2 (.D(multiplexer_2_out), .en(or_2_out), .clk(CLK), .Q(R1));  // open: clr
  Multiplexer #(.width(16)) multiplexer_2 (.in0(I_S1), .in1(I_P1), .out(multiplexer_2_out), .sel(WE_P1));
  or or_2 (or_2_out, WE_S1, WE_P1);
  Register #(.width(16)) register_3 (.D(multiplexer_3_out), .en(or_3_out), .clk(CLK), .Q(R2));  // open: clr
  Multiplexer #(.width(16)) multiplexer_3 (.in0(I_S2), .in1(I_P2), .out(multiplexer_3_out), .sel(WE_P2));
  or or_3 (or_3_out, WE_S2, WE_P2);
  Register #(.width(16)) register_4 (.D(multiplexer_4_out), .en(or_4_out), .clk(CLK), .Q(R3));  // open: clr
  Multiplexer #(.width(16)) multiplexer_4 (.in0(I_S3), .in1(I_P3), .out(multiplexer_4_out), .sel(WE_P3));
  or or_4 (or_4_out, WE_S3, WE_P3);
  Register #(.width(16)) register_5 (.D(multiplexer_5_out), .en(or_5_out), .clk(CLK), .Q(R4));  // open: clr
  Multiplexer #(.width(16)) multiplexer_5 (.in0(I_S4), .in1(I_P4), .out(multiplexer_5_out), .sel(WE_P4));
  or or_5 (or_5_out, WE_S4, WE_P4);
  Register #(.width(16)) register_6 (.D(multiplexer_6_out), .en(or_6_out), .clk(CLK), .Q(R5));  // open: clr
  Multiplexer #(.width(16)) multiplexer_6 (.in0(I_S5), .in1(I_P5), .out(multiplexer_6_out), .sel(WE_P5));
  or or_6 (or_6_out, WE_S5, WE_P5);
  Register #(.width(16)) register_7 (.D(multiplexer_7_out), .en(or_7_out), .clk(CLK), .Q(R6));  // open: clr
  Multiplexer #(.width(16)) multiplexer_7 (.in0(I_S6), .in1(I_P6), .out(multiplexer_7_out), .sel(WE_P6));
  or or_7 (or_7_out, WE_S6, WE_P6);
  Register #(.width(16)) register_8 (.D(multiplexer_8_out), .en(or_8_out), .clk(CLK), .Q(R7));  // open: clr
  Multiplexer #(.width(16)) multiplexer_8 (.in0(I_S7), .in1(I_P7), .out(multiplexer_8_out), .sel(WE_P7));
  or or_8 (or_8_out, WE_S7, WE_P7);
endmodule

module JC16_16bit_8bit_stepdown (
  input  [15:0] A,
  output [7:0] R
);


  assign R = A[7:0];
endmodule

module JC16_ALU_Input_Handler (
  input  [1:0] FLAG,
  input  [7:0] ELABORATE_BODY,
  input  [15:0] I_R0,
  input  [15:0] I_R1,
  input  [15:0] I_R2,
  input  [15:0] I_R3,
  input  [15:0] I_R4,
  input  [15:0] I_R5,
  input  [15:0] I_R6,
  input  [15:0] I_R7,
  input  [2:0] REG_A,
  input  [2:0] REG_B,
  output [15:0] O_A,
  output [15:0] O_B
);

  wire and_1_out, and_2_out, and_3_out, and_4_out, not_1_out, not_2_out, not_3_out, not_4_out, not_5_out,
       not_6_out, not_7_out;
  wire [15:0] jc16_8bit_16bit_stepup_1_r, jcs1_alu_1_r, multiplexer_1_out, multiplexer_2_out,
       multiplexer_3_out, multiplexer_4_out, multiplexer_5_out, multiplexer_6_out, multiplexer_7_out;

  Multiplexer #(.select(3), .width(16)) multiplexer_1 (
    .in0(I_R0), .in1(I_R1), .in2(I_R2), .in3(I_R3), .in4(I_R4), .in5(I_R5), .in6(I_R6), .in7(I_R7),
    .out(multiplexer_1_out), .sel(REG_A));
  Multiplexer #(.select(3), .width(16)) multiplexer_2 (
    .in0(I_R0), .in1(I_R1), .in2(I_R2), .in3(I_R3), .in4(I_R4), .in5(I_R5), .in6(I_R6), .in7(I_R7),
    .out(multiplexer_2_out));  // open: sel
  Multiplexer #(.select(3), .width(16)) multiplexer_3 (
    .in0(I_R0), .in1(I_R1), .in2(I_R2), .in3(I_R3), .in4(I_R4), .in5(I_R5), .in6(I_R6), .in7(I_R7),
    .out(multiplexer_3_out), .sel(REG_B));
  not not_1 (not_1_out, FLAG[0]);
  JC16_8bit_16bit_stepup jc16_8bit_16bit_stepup_1 (.A(ELABORATE_BODY), .R(jc16_8bit_16bit_stepup_1_r));
  Multiplexer #(.width(16)) multiplexer_4 (
    .in0(multiplexer_3_out), .in1(multiplexer_1_out), .out(multiplexer_4_out), .sel(not_1_out));
  and and_1 (and_1_out, FLAG[1], not_2_out);
  not not_2 (not_2_out, FLAG[0]);
  and and_2 (and_2_out, FLAG[1], FLAG[0]);
  Multiplexer #(.width(16)) multiplexer_5 (
    .in0(multiplexer_1_out), .in1(jcs1_alu_1_r), .out(multiplexer_5_out), .sel(and_3_out));
  Multiplexer #(.width(16)) multiplexer_6 (
    .in0(multiplexer_3_out), .in1(jcs1_alu_1_r), .out(multiplexer_6_out), .sel(and_4_out));
  Multiplexer #(.width(16)) multiplexer_7 (
    .in0(multiplexer_2_out), .in1({{13{1'b0}}, ELABORATE_BODY[3:1]}), .out(multiplexer_7_out),
    .sel(ELABORATE_BODY[0]));
  not not_3 (not_3_out, FLAG[0]);
  Multiplexer #(.width(16)) multiplexer_8 (
    .in0(jc16_8bit_16bit_stepup_1_r), .in1(multiplexer_5_out), .out(O_A), .sel(not_4_out));
  not not_4 (not_4_out, and_1_out);
  Multiplexer #(.width(16)) multiplexer_9 (
    .in0(jc16_8bit_16bit_stepup_1_r), .in1(multiplexer_6_out), .out(O_B), .sel(not_5_out));
  not not_5 (not_5_out, and_2_out);
  and and_3 (and_3_out, not_3_out, not_7_out);
  and and_4 (and_4_out, not_6_out, FLAG[0]);
  not not_6 (not_6_out, FLAG[0]);
  not not_7 (not_7_out, FLAG[0]);
  JCS1_ALU jcs1_alu_1 (
    .F(ELABORATE_BODY[7:4]), .A(multiplexer_4_out), .B(multiplexer_7_out), .R(jcs1_alu_1_r));  // open: Carry
endmodule

module JC16_8bit_16bit_stepup (
  input  [7:0] A,
  output [15:0] R
);


  assign R = {{8{1'b0}}, A};
endmodule

module JC16_Parallelism_Detection (
  input  [23:0] INSTR_A,
  input  [23:0] INSTR_B,
  output CAN_RUN_PARALLEL
);

  wire and_1_out, and_2_out, CHECK_IF_LDI_out, jc16_register_comparison_1_is_equal,
       jc16_register_comparison_2_is_equal, jc16_register_comparison_3_is_equal, nand_1_out, nor_1_out,
       not_1_out, not_2_out, not_3_out, or_1_out, or_2_out;

  JC16_Register_Comparison jc16_register_comparison_1 (
    .R1(INSTR_A[18:16]), .R2(INSTR_B[15:13]), .IS_EQUAL(jc16_register_comparison_1_is_equal));
  JC16_Register_Comparison jc16_register_comparison_2 (
    .R1(INSTR_A[18:16]), .R2(INSTR_B[12:10]), .IS_EQUAL(jc16_register_comparison_2_is_equal));
  nor nor_1 (nor_1_out, jc16_register_comparison_1_is_equal, jc16_register_comparison_2_is_equal);
  JC16_Register_Comparison jc16_register_comparison_3 (
    .R1(INSTR_A[18:16]), .R2(INSTR_B[3:1]), .IS_EQUAL(jc16_register_comparison_3_is_equal));
  or CHECK_IF_LDI (CHECK_IF_LDI_out, INSTR_A[19], INSTR_A[20], INSTR_A[21], not_1_out);
  not not_1 (not_1_out, INSTR_A[22]);
  not not_2 (not_2_out, INSTR_B[23]);
  or or_1 (or_1_out, INSTR_B[9], INSTR_B[0], or_2_out);
  not not_3 (not_3_out, jc16_register_comparison_3_is_equal);
  or or_2 (or_2_out, not_3_out, and_1_out);
  and and_1 (and_1_out, INSTR_B[4], INSTR_B[5], INSTR_B[7], INSTR_B[6]);
  and and_2 (and_2_out, CHECK_IF_LDI_out, INSTR_A[23]);
  nand nand_1 (nand_1_out, nor_1_out, not_2_out, or_1_out);
  nor nor_2 (CAN_RUN_PARALLEL, and_2_out, nand_1_out);
endmodule

module JC16_Register_Comparison (
  input  [2:0] R1,
  input  [2:0] R2,
  output IS_EQUAL
);

  wire [2:0] xor_1_out;

  assign xor_1_out = R1 ^ R2;  // XOR_Gate xor_1, 3 bits wide
  nor nor_1 (IS_EQUAL, xor_1_out[0], xor_1_out[1], xor_1_out[2]);
endmodule

module JC16_Tiny_Instruction_Decoder (
  input  [23:0] INSTR,
  output IS_ALU,
  output [3:0] ALU_F,
  output [2:0] TARGET_REG,
  output [2:0] REG_A,
  output [2:0] REG_B,
  output [1:0] FLAG,
  output [7:0] ALU_BODY
);

  not not_1 (IS_ALU, INSTR[23]);

  assign ALU_BODY = INSTR[7:0];
  assign ALU_F = INSTR[22:19];
  assign FLAG = INSTR[9:8];
  assign REG_A = INSTR[15:13];
  assign REG_B = INSTR[12:10];
  assign TARGET_REG = INSTR[18:16];
endmodule
